// Logisim project pc_simulation.circ as structural Verilog: 1 circuit, main circuit main
module main (
  input  interrupt
);

  wire adder_4_cout, adr_CD, adr_inc, adr_L, adr_PC, adr_SP, and_1_out, and_3_out, and_8_out, and_9_out,
       and_10_out, and_11_out, and_12_out, and_14_out, and_15_out, and_16_out, and_19_out, and_20_out,
       CARRY_FLAG, clk, clock_1_out, comparator_1_eq, comparator_2_eq, comparator_3_eq, comparator_3_lt,
       d_ff_1_qn, d_ff_2_q, decoder_1_out0, decoder_2_out0, decoder_2_out1, decoder_2_out2, decoder_3_out1,
       decoder_3_out2, decoder_3_out3, decoder_3_out4, decoder_3_out6, decoder_7_out0, decoder_7_out1,
       decoder_7_out2, decoder_7_out3, decoder_7_out4, decoder_7_out5, halt, halted, MINUS_FLAG, nand_1_out,
       not_1_out, not_2_out, not_3_out, not_4_out, not_5_out, not_8_out, or_1_out, or_3_out, read_A,
       read_ALU, read_B, read_C, read_D, read_L1, read_L2, read_MEM, read_PCH, read_PCL, read_SPH, read_SPL,
       RESET, shift_register_1_p5, shift_register_1_p6, shift_register_1_p7, shift_register_1_p8,
       shift_register_1_p9, shift_register_1_p10, shift_register_1_p11, shift_register_1_p12,
       shift_register_1_p13, shift_register_1_p14, shift_register_1_p15, shift_register_1_p16, undriven,
       undriven_2, undriven_3, undriven_4, write_A, write_ALU, write_B, write_C, write_D, write_IPC,
       write_L1, write_L2, write_MEM, write_PC, write_SP, xor_3_out, xor_4_out, ZERO_FLAG;
  wire [2:0] adr_src, data_target, register_2_q;
  wire [3:0] adder_1_out, alu_command, and_4_out, bit_extender_1_out, data_source, step;
  wire [4:4] microcode_high_data;
  wire [7:0] adder_4_out, ALU_IN_q, and_13_out, and_18_out, bit_extender_5_out, bit_extender_6_out,
       bit_extender_7_out, controlled_buffer_1_out, data, instruction, nor_1_out, not_7_out, or_2_out,
       or_4_out, PROGRAM_data, reg_A_direct, REG_B_q, REG_C_q, REG_D_q, reg_L1_direct, REG_L2_q,
       register_1_q, xor_2_out;
  wire [7:7] microcode_low_data;
  wire [15:0] adder_3_out, address, and_17_out, bit_extender_2_out, bit_extender_3_out, bit_extender_4_out,
       INCR_q, ipc, PC_q, register_4_q, SP_q, xor_1_out;
  wire [31:0] adder_2_out, register_3_q;

  not not_1 (not_1_out, interrupt);
  assign controlled_buffer_1_out = not_1_out ? data : 8'bz;  // Controlled_Buffer controlled_buffer_1
  assign controlled_buffer_1_out = interrupt ? 8'hf0 : 8'bz;  // Controlled_Buffer controlled_buffer_2
  Register register_1 (.D(controlled_buffer_1_out), .clk(and_1_out), .Q(register_1_q), .clr(RESET));  // open: en
  Clock clock_1 (.out(clock_1_out));
  not not_2 (not_2_out, clk);
  not not_3 (not_3_out, and_1_out);
  nand nand_1 (nand_1_out, d_ff_1_qn, clock_1_out);
  not not_4 (not_4_out, nand_1_out);
  and and_1 (and_1_out, ~step[0], ~step[1], ~step[2], ~step[3], clk);  // AND_Gate
  Register #(.width(3)) register_2 (
    .D({MINUS_FLAG, ZERO_FLAG, CARRY_FLAG}), .clk(not_2_out), .Q(register_2_q));  // open: en, clr
  Register IR (.D(register_1_q), .clk(not_3_out), .Q(instruction), .clr(RESET));  // open: en
  D_Flip_Flop d_ff_1 (.D(halt), .clk(not_4_out), .Q(halted), .Qn(d_ff_1_qn), .reset(RESET));  // open: preset
  D_Flip_Flop d_ff_2 (.D(1'b1), .clk(nand_1_out), .Q(d_ff_2_q), .reset(RESET));  // open: Qn, preset
  LED led_1 (.in(halted));
  Adder #(.width(4)) adder_1 (.a(step), .b(4'b0000), .out(adder_1_out), .cin(1'b1));  // open: cout
  assign bit_extender_1_out = {{3{microcode_low_data[7]}}, microcode_low_data[7]};  // Bit_Extender bit_extender_1
  and and_2 (clk, not_4_out, d_ff_2_q);
  ROM #(.addrWidth(15)) microcode_low (
    .addr({step, register_2_q, instruction}), .data({microcode_low_data[7], data_target, data_source}));
  ROM #(.addrWidth(15)) microcode_high (
    .addr({step, register_2_q, instruction}), .data({adr_src, microcode_high_data[4], alu_command}));
  ROM #(.addrWidth(13)) PROGRAM (.addr(address[12:0]), .data(PROGRAM_data));
  Comparator #(.width(16)) comparator_1 (.a(16'h2000), .b(address), .eq(comparator_1_eq));  // open: gt, lt
  and and_3 (and_3_out, write_MEM, clk);
  Register #(.width(4)) SEQUENCER (.D(and_4_out), .clk(not_5_out), .Q(step), .clr(RESET));  // open: en
  assign and_4_out = adder_1_out & bit_extender_1_out;  // AND_Gate and_4, 4 bits wide
  not not_5 (not_5_out, clk);
  // Shift_Register #(.length(16), .width(8)) shift_register_1: pin names not known; wires that end beside it: RESET, comparator_1_eq, and_3_out, data, shift_register_1_p5, shift_register_1_p6, shift_register_1_p7, shift_register_1_p8, shift_register_1_p9, shift_register_1_p10, shift_register_1_p11, shift_register_1_p12, shift_register_1_p13, shift_register_1_p14, shift_register_1_p15, shift_register_1_p16
  // Probe on shift_register_1_p5
  // Probe on shift_register_1_p6
  // Probe on shift_register_1_p7
  // Probe on shift_register_1_p8
  // Probe on shift_register_1_p9
  // Probe on shift_register_1_p10
  // Probe on shift_register_1_p11
  // Probe on shift_register_1_p12
  // Probe on shift_register_1_p13
  // Probe on shift_register_1_p14
  // Probe on shift_register_1_p15
  // Probe on shift_register_1_p16
  // Probe on undriven
  // Probe on undriven_2
  // Probe on undriven_3
  // Probe on undriven_4
  assign data = decoder_1_out0 ? PROGRAM_data : 8'bz;  // Controlled_Buffer controlled_buffer_3
  Hex_Digit_Display #(.decimalPoint("false")) hex_digit_display_1 (.value(instruction[7:4]));
  Decoder #(.select(3)) decoder_1 (
    .out0(decoder_1_out0), .sel(address[15:13]), .en(read_MEM));  // open: out1, out2, out3, out4, out5, out6, out7
  Button button_1 (.out(RESET));
  Hex_Digit_Display #(.decimalPoint("false")) hex_digit_display_2 (.value(instruction[3:0]));
  Hex_Digit_Display #(.decimalPoint("false")) hex_digit_display_3 (.value(step));
  Decoder #(.select(4)) decoder_2 (
    .out0(decoder_2_out0), .out1(decoder_2_out1), .out2(decoder_2_out2), .out8(halt), .sel(alu_command),
    .en(microcode_high_data[4]));  // open: out3, out4, out5, out6, out7, out9, out10, out11, out12, out13, out14, out15
  and and_5 (write_SP, clk, decoder_2_out1);
  and and_6 (write_PC, clk, decoder_2_out0);
  and and_7 (write_IPC, clk, decoder_2_out2);
  Decoder #(.enable("false"), .select(3)) decoder_3 (
    .out1(decoder_3_out1), .out2(decoder_3_out2), .out3(decoder_3_out3), .out4(decoder_3_out4),
    .out6(decoder_3_out6), .sel(data_target));  // open: out0, out5, out7
  Comparator #(.width(4)) comparator_2 (.a(data_source), .b(4'b1110), .eq(comparator_2_eq));  // open: gt, lt
  and and_8 (and_8_out, read_MEM, address[15]);
  and and_9 (and_9_out, address[15], write_MEM);
  LED led_2 (.in(halted));
  Hex_Digit_Display #(.decimalPoint("false")) hex_digit_display_4 (.value(data[7:4]));
  Hex_Digit_Display #(.decimalPoint("false")) hex_digit_display_5 (.value(data[3:0]));
  or or_1 (or_1_out, decoder_3_out1, decoder_3_out2, decoder_3_out3, decoder_3_out4, and_10_out);
  and and_10 (and_10_out, ~decoder_3_out6, comparator_2_eq);  // AND_Gate
  RAM #(.addrWidth(15), .asyncread("true"), .databus("bidir"), .\type ("nonvolatile")) ram_1 (
    .addr(address[14:0]), .we(1'b1), .oe(and_8_out), .clk(and_9_out), .data(data));
  Hex_Digit_Display #(.decimalPoint("false")) hex_digit_display_6 (.value(address[15:12]));
  Decoder #(.enable("false"), .select(4)) decoder_4 (
    .out1(read_A), .out2(read_B), .out3(read_C), .out4(read_D), .out5(read_L1), .out6(read_L2),
    .out8(read_PCL), .out9(read_PCH), .out10(read_SPL), .out11(read_SPH), .out14(read_ALU), .out15(read_MEM),
    .sel(data_source));  // open: out0, out7, out12, out13
  and and_11 (and_11_out, or_1_out, clk);
  Hex_Digit_Display #(.decimalPoint("false")) hex_digit_display_7 (.value(address[11:8]));
  Hex_Digit_Display #(.decimalPoint("false")) hex_digit_display_8 (.value(address[7:4]));
  Register #(.width(1)) FLAG_Z (.D(comparator_3_eq), .clk(and_11_out), .Q(ZERO_FLAG), .clr(RESET));  // open: en
  Comparator comparator_3 (.a(data), .b({8{1'b0}}), .eq(comparator_3_eq), .lt(comparator_3_lt));  // open: gt
  Register #(.width(1)) FLAG_S (.D(comparator_3_lt), .clk(and_11_out), .Q(MINUS_FLAG), .clr(RESET));  // open: en
  Hex_Digit_Display #(.decimalPoint("false")) hex_digit_display_9 (.value(address[3:0]));
  // Probe on clk
  // Probe on data_source
  // Probe on data_target
  // Probe on adr_src
  // Probe on {microcode_high_data[4], alu_command}
  Pull_Resistor #(.pull(1)) pull_resistor_1 (.node(data));
  Pull_Resistor pull_resistor_2 (.node(address));
  Register #(.width(32)) register_3 (.D(adder_2_out), .clk(clk), .Q(register_3_q), .clr(RESET));  // open: en
  Adder #(.width(32)) adder_2 (.a(register_3_q), .b(32'h1), .out(adder_2_out));  // open: cin, cout
  // Probe on register_3_q
  Decoder #(.select(3)) decoder_5 (
    .out0(write_ALU), .out1(write_A), .out2(write_B), .out3(write_C), .out4(write_D), .out5(write_L1),
    .out6(write_L2), .out7(write_MEM), .sel(data_target), .en(clk));
  Decoder #(.enable("false"), .select(3)) decoder_6 (
    .out4(adr_L), .out5(adr_CD), .out6(adr_PC), .out7(adr_SP), .sel(adr_src));  // open: out0, out1, out2, out3
  Register REG_A (.D(data), .clk(write_A), .Q(reg_A_direct), .clr(RESET));  // open: en
  Register REG_B (.D(data), .clk(write_B), .Q(REG_B_q), .clr(RESET));  // open: en
  Register REG_C (.D(data), .clk(write_C), .Q(REG_C_q), .clr(RESET));  // open: en
  Register REG_D (.D(data), .clk(write_D), .Q(REG_D_q), .clr(RESET));  // open: en
  Register REG_L1 (.D(data), .clk(write_L1), .Q(reg_L1_direct), .clr(RESET));  // open: en
  Register REG_L2 (.D(data), .clk(write_L2), .Q(REG_L2_q), .clr(RESET));  // open: en
  not not_6 (adr_inc, adr_src[2]);
  assign data = read_A ? reg_A_direct : 8'bz;  // Controlled_Buffer controlled_buffer_4
  assign data = read_B ? REG_B_q : 8'bz;  // Controlled_Buffer controlled_buffer_5
  assign data = read_C ? REG_C_q : 8'bz;  // Controlled_Buffer controlled_buffer_6
  assign data = read_D ? REG_D_q : 8'bz;  // Controlled_Buffer controlled_buffer_7
  assign data = read_L1 ? reg_L1_direct : 8'bz;  // Controlled_Buffer controlled_buffer_8
  assign data = read_L2 ? REG_L2_q : 8'bz;  // Controlled_Buffer controlled_buffer_9
  assign address = adr_CD ? {REG_D_q, REG_C_q} : 16'bz;  // Controlled_Buffer controlled_buffer_10
  assign address = adr_L ? {REG_L2_q, reg_L1_direct} : 16'bz;  // Controlled_Buffer controlled_buffer_11
  Register #(.width(16)) u_IPC (.D(address), .clk(write_IPC), .Q(ipc), .clr(RESET));  // open: en
  Register ALU_IN (.D(data), .clk(write_ALU), .Q(ALU_IN_q));  // open: en, clr
  Register #(.width(16)) PC (.D(address), .clk(write_PC), .Q(PC_q), .clr(RESET));  // open: en
  Register #(.width(16)) SP (.D(address), .clk(write_SP), .Q(SP_q), .clr(RESET));  // open: en
  assign address = adr_PC ? PC_q : 16'bz;  // Controlled_Buffer controlled_buffer_12
  assign data = read_PCL ? PC_q[7:0] : 8'bz;  // Controlled_Buffer controlled_buffer_13
  assign data = read_PCH ? PC_q[15:8] : 8'bz;  // Controlled_Buffer controlled_buffer_14
  assign address = adr_SP ? SP_q : 16'bz;  // Controlled_Buffer controlled_buffer_15
  assign data = read_SPL ? SP_q[7:0] : 8'bz;  // Controlled_Buffer controlled_buffer_16
  assign data = read_SPH ? SP_q[15:8] : 8'bz;  // Controlled_Buffer controlled_buffer_17
  and and_12 (and_12_out, read_ALU, ~alu_command[3]);  // AND_Gate
  assign not_7_out = ~ALU_IN_q;  // NOT_Gate not_7, 8 bits wide
  assign and_13_out = ALU_IN_q & reg_A_direct;  // AND_Gate and_13, 8 bits wide
  assign data = decoder_7_out0 ? and_13_out : 8'bz;  // Controlled_Buffer controlled_buffer_18
  assign or_2_out = ALU_IN_q | reg_A_direct;  // OR_Gate or_2, 8 bits wide
  assign data = decoder_7_out1 ? or_2_out : 8'bz;  // Controlled_Buffer controlled_buffer_19
  assign nor_1_out = ~(ALU_IN_q | reg_A_direct);  // NOR_Gate nor_1, 8 bits wide
  assign data = decoder_7_out2 ? nor_1_out : 8'bz;  // Controlled_Buffer controlled_buffer_20
  assign data = decoder_7_out3 ? not_7_out : 8'bz;  // Controlled_Buffer controlled_buffer_21
  assign data = decoder_7_out4 ? {CARRY_FLAG, ALU_IN_q[7:1]} : 8'bz;  // Controlled_Buffer controlled_buffer_22
  assign data = decoder_7_out5 ? {ALU_IN_q[6:0], CARRY_FLAG} : 8'bz;  // Controlled_Buffer controlled_buffer_23
  Decoder #(.select(3)) decoder_7 (
    .out0(decoder_7_out0), .out1(decoder_7_out1), .out2(decoder_7_out2), .out3(decoder_7_out3),
    .out4(decoder_7_out4), .out5(decoder_7_out5), .sel(alu_command[2:0]), .en(and_12_out));  // open: out6, out7
  and and_14 (and_14_out, ALU_IN_q[0], decoder_7_out4);
  and and_15 (and_15_out, decoder_7_out5, ALU_IN_q[7]);
  Register #(.width(16)) register_4 (.D(address), .clk(clk), .Q(register_4_q));  // open: en, clr
  or or_3 (or_3_out, and_20_out, and_14_out, and_15_out);
  and and_16 (and_16_out, read_ALU, clk);
  assign bit_extender_2_out = {{15{adr_src[0]}}, adr_src[0]};  // Bit_Extender bit_extender_2
  assign bit_extender_3_out = {{15{adr_src[1]}}, adr_src[1]};  // Bit_Extender bit_extender_3
  assign bit_extender_4_out = {{8{1'b0}}, reg_L1_direct};  // Bit_Extender bit_extender_4
  Register #(.width(16)) INCR (.D(register_4_q), .clk(not_8_out), .Q(INCR_q));  // open: en, clr
  not not_8 (not_8_out, clk);
  Register #(.width(1)) FLAG_C (.D(or_3_out), .clk(and_16_out), .Q(CARRY_FLAG));  // open: en, clr
  assign and_17_out = bit_extender_3_out & bit_extender_4_out;  // AND_Gate and_17, 16 bits wide
  assign bit_extender_5_out = {{7{alu_command[0]}}, alu_command[0]};  // Bit_Extender bit_extender_5
  assign bit_extender_6_out = {{7{alu_command[1]}}, alu_command[1]};  // Bit_Extender bit_extender_6
  assign and_18_out = bit_extender_6_out & reg_A_direct;  // AND_Gate and_18, 8 bits wide
  assign bit_extender_7_out = {{7{alu_command[2]}}, alu_command[2]};  // Bit_Extender bit_extender_7
  assign xor_1_out = bit_extender_2_out ^ and_17_out;  // XOR_Gate xor_1, 16 bits wide
  assign xor_2_out = ALU_IN_q ^ bit_extender_5_out;  // XOR_Gate xor_2, 8 bits wide
  assign or_4_out = and_18_out | bit_extender_7_out;  // OR_Gate or_4, 8 bits wide
  xor xor_3 (xor_3_out, adr_src[1], adr_src[0]);
  xor xor_4 (xor_4_out, xor_3_out, 1'b1);
  // Probe on adder_3_out
  Adder #(.width(16)) adder_3 (.a(xor_1_out), .b(INCR_q), .out(adder_3_out), .cin(xor_4_out));  // open: cout
  and and_19 (and_19_out, alu_command[3], read_ALU);
  assign data = and_19_out ? adder_4_out : 8'bz;  // Controlled_Buffer controlled_buffer_24
  Adder adder_4 (.a(xor_2_out), .b(or_4_out), .out(adder_4_out), .cin(CARRY_FLAG), .cout(adder_4_cout));
  and and_20 (and_20_out, adder_4_cout, alu_command[3]);
  assign address = adr_inc ? adder_3_out : 16'bz;  // Controlled_Buffer controlled_buffer_25

  // Other names for the same wires on the sheet: inc_dec = adr_src[0]; inc_offset = adr_src[1]

  // Notes on the sheet:
  //   contents of microcode_low (hex, n*v repeats v):
  //   7*8f 0 7*8f 0 7*8f 0 7*8f 0 7*8f 0 7*8f 0 21*8f 0 0 0 6*8f 0 0 8*8f 8*0 64*8f 16*0 9*8f 0 8f 8f 64*0
  //   11*8f 0 7*8f 0 7*8f 0 7*8f 0 7*8f 0 7*8f 0 21*8f 0 0 0 6*8f 0 0 8*8f 8*0 64*8f 16*0 9*8f 0 8f 8f
  //   64*0 11*8f 0 7*8f 0 7*8f 0 7*8f 0 7*8f 0 7*8f 0 21*8f 0 0 0 6*8f 0 0 8*8f 8*0 64*8f 16*0 9*8f 0 8f
  //   8f 64*0 11*8f 0 7*8f 0 7*8f 0 7*8f 0 7*8f 0 7*8f 0 21*8f 0 0 0 6*8f 0 0 8*8f 8*0 64*8f 16*0 9*8f 0
  //   8f 8f 64*0 11*8f 0 7*8f 0 7*8f 0 7*8f 0 7*8f 0 7*8f 0 21*8f 0 0 0 6*8f 0 0 8*8f 8*0 64*8f 16*0 9*8f
  //   0 8f 8f 64*0 11*8f 0 7*8f 0 7*8f 0 7*8f 0 7*8f 0 7*8f 0 21*8f 0 0 0 6*8f 0 0 8*8f 8*0 64*8f 16*0
  //   9*8f 0 8f 8f 64*0 4*8f 512*0 82 83 84 8f df df df 0 82 83 84 8f df df df 0 82 83 84 8f df df df 0 82
  //   83 84 8f df df df 0 82 83 84 8f df df df 0 80 80 80 4*df 0 81 82 83 84 81 82 83 84 81 82 83 84 81 82
  //   83 84 4*81 80 0 0 0 82 83 84 df df df 0 0 8*df 8*0 11 12 13 14 21 22 23 24 31 32 33 34 41 42 43 44
  //   12*df 9f af bf cf 16*df 0 93 b1 0 6*df 9f bf 4*df 16*0 9*df 0 df df 64*0 80 80 0 0 82 83 84 8f df df
  //   df 0 82 83 84 8f df df df 0 82 83 84 8f df df df 0 82 83 84 8f df df df 0 82 83 84 8f df df df 0 80
  //   80 80 4*df 0 81 82 83 84 81 82 83 84 81 82 83 84 81 82 83 84 4*81 80 0 0 0 82 83 84 df df df 0 0
  //   8*df 8*0 11 12 13 14 21 22 23 24 31 32 33 34 41 42 43 44 12*df 9f af bf cf 16*df 0 93 b1 0 6*df 9f
  //   bf 4*df 16*0 9*df 0 df df 64*0 80 80 0 0 82 83 84 8f df df df 0 82 83 84 8f df df df 0 82 83 84 8f
  //   df df df 0 82 83 84 8f df df df 0 82 83 84 8f df df df 0 80 80 80 4*df 0 81 82 83 84 81 82 83 84 81
  //   82 83 84 81 82 83 84 4*81 80 0 0 0 82 83 84 df df df 0 0 8*df 8*0 11 12 13 14 21 22 23 24 31 32 33
  //   34 41 42 43 44 12*df 9f af bf cf 16*df 0 93 b1 0 6*df 9f bf 4*df 16*0 9*df 0 df df 64*0 80 80 0 0 82
  //   83 84 8f df df df 0 82 83 84 8f df df df 0 82 83 84 8f df df df 0 82 83 84 8f df df df 0 82 83 84 8f
  //   df df df 0 80 80 80 4*df 0 81 82 83 84 81 82 83 84 81 82 83 84 81 82 83 84 4*81 80 0 0 0 82 83 84 df
  //   df df 0 0 8*df 8*0 11 12 13 14 21 22 23 24 31 32 33 34 41 42 43 44 12*df 9f af bf cf 16*df 0 93 b1 0
  //   6*df 9f bf 4*df 16*0 9*df 0 df df 64*0 80 80 0 0 82 83 84 8f df df df 0 82 83 84 8f df df df 0 82 83
  //   84 8f df df df 0 82 83 84 8f df df df 0 82 83 84 8f df df df 0 80 80 80 4*df 0 81 82 83 84 81 82 83
  //   84 81 82 83 84 81 82 83 84 4*81 80 0 0 0 82 83 84 df df df 0 0 8*df 8*0 11 12 13 14 21 22 23 24 31
  //   32 33 34 41 42 43 44 12*df 9f af bf cf 16*df 0 93 b1 0 6*df 9f bf 4*df 16*0 9*df 0 df df 64*0 80 80
  //   0 0 82 83 84 8f df df df 0 82 83 84 8f df df df 0 82 83 84 8f df df df 0 82 83 84 8f df df df 0 82
  //   83 84 8f df df df 0 80 80 80 4*df 0 81 82 83 84 81 82 83 84 81 82 83 84 81 82 83 84 4*81 80 0 0 0 82
  //   83 84 df df df 0 0 8*df 8*0 11 12 13 14 21 22 23 24 31 32 33 34 41 42 43 44 12*df 9f af bf cf 16*df
  //   0 93 b1 0 6*df 9f bf 4*df 16*0 9*df 0 df df 64*0 80 80 514*0 1e 1e 1e e5 ef 80 80 0 1e 1e 1e e5 ef
  //   80 80 0 1e 1e 1e e5 ef 80 80 0 1e 1e 1e e5 ef 80 80 0 1e 1e 1e e5 ef 80 80 0 8e 8e 8e 80 ef 80 80 0
  //   1e 2e 3e 4e 1e 2e 3e 4e 1e 2e 3e 4e 1e 2e 3e 4e 1e 9e 1e 9e 8e 0 0 0 a1 b1 c1 ef 80 80 0 0 8*80 24*0
  //   4*ef 8*80 4*0 4*ef 8*80 ef ef 80 80 0 24 42 0 ef ef 4*80 af cf 4*80 16*0 9*ef 0 ef ef 64*0 6e 6e 0 0
  //   1e 1e 1e e5 ef 80 80 0 1e 1e 1e e5 ef 80 80 0 1e 1e 1e e5 ef 80 80 0 1e 1e 1e e5 ef 80 80 0 1e 1e 1e
  //   e5 ef 80 80 0 8e 8e 8e 80 ef 80 80 0 1e 2e 3e 4e 1e 2e 3e 4e 1e 2e 3e 4e 1e 2e 3e 4e 1e 9e 1e 9e 8e
  //   0 0 0 a1 b1 c1 ef 80 80 0 0 8*80 24*0 4*ef 8*80 4*0 4*ef 8*80 ef ef 80 80 0 24 42 0 ef ef 4*80 af cf
  //   4*80 16*0 9*ef 0 ef ef 64*0 6e 6e 0 0 1e 1e 1e e5 ef 80 80 0 1e 1e 1e e5 ef 80 80 0 1e 1e 1e e5 ef
  //   80 80 0 1e 1e 1e e5 ef 80 80 0 1e 1e 1e e5 ef 80 80 0 8e 8e 8e 80 ef 80 80 0 1e 2e 3e 4e 1e 2e 3e 4e
  //   1e 2e 3e 4e 1e 2e 3e 4e 1e 9e 1e 9e 8e 0 0 0 a1 b1 c1 ef 80 80 0 0 8*80 24*0 4*ef 8*80 4*0 4*ef 8*80
  //   ef ef 80 80 0 24 42 0 ef ef 4*80 af cf 4*80 16*0 9*ef 0 ef ef 64*0 6e 6e 0 0 1e 1e 1e e5 ef 80 80 0
  //   1e 1e 1e e5 ef 80 80 0 1e 1e 1e e5 ef 80 80 0 1e 1e 1e e5 ef 80 80 0 1e 1e 1e e5 ef 80 80 0 8e 8e 8e
  //   80 ef 80 80 0 1e 2e 3e 4e 1e 2e 3e 4e 1e 2e 3e 4e 1e 2e 3e 4e 1e 9e 1e 9e 8e 0 0 0 a1 b1 c1 ef 80 80
  //   0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
  //   contents of microcode_high (hex, n*v repeats v):
  //   7*c0 18 7*c0 18 7*c0 18 7*c0 18 7*c0 18 7*c0 18 21*c0 18 18 18 6*c0 18 18 8*c0 8*18 64*c0 16*18 9*c0
  //   18 c0 c0 64*18 11*c0 18 7*c0 18 7*c0 18 7*c0 18 7*c0 18 7*c0 18 21*c0 18 18 18 6*c0 18 18 8*c0 8*18
  //   64*c0 16*18 9*c0 18 c0 c0 64*18 11*c0 18 7*c0 18 7*c0 18 7*c0 18 7*c0 18 7*c0 18 21*c0 18 18 18 6*c0
  //   18 18 8*c0 8*18 64*c0 16*18 9*c0 18 c0 c0 64*18 11*c0 18 7*c0 18 7*c0 18 7*c0 18 7*c0 18 7*c0 18
  //   21*c0 18 18 18 6*c0 18 18 8*c0 8*18 64*c0 16*18 9*c0 18 c0 c0 64*18 11*c0 18 7*c0 18 7*c0 18 7*c0 18
  //   7*c0 18 7*c0 18 21*c0 18 18 18 6*c0 18 18 8*c0 8*18 64*c0 16*18 9*c0 18 c0 c0 64*18 11*c0 18 7*c0 18
  //   7*c0 18 7*c0 18 7*c0 18 7*c0 18 21*c0 18 18 18 6*c0 18 18 8*c0 8*18 64*c0 16*18 9*c0 18 c0 c0 64*18
  //   4*c0 512*18 10 10 10 4*0 18 10 10 10 4*0 18 10 10 10 4*0 18 10 10 10 4*0 18 10 10 10 4*0 18 10 10 10
  //   4*0 18 21*10 18 18 18 10 10 10 0 0 0 18 18 8*0 8*18 16*10 32*0 4*10 12*0 16*18 9*0 18 0 e0 64*18 10
  //   10 10 18 10 10 10 4*0 18 10 10 10 4*0 18 10 10 10 4*0 18 10 10 10 4*0 18 10 10 10 4*0 18 10 10 10
  //   4*0 18 21*10 18 18 18 10 10 10 0 0 0 18 18 8*0 8*18 16*10 32*0 4*10 12*0 16*18 9*0 18 0 e0 64*18 10
  //   10 10 18 10 10 10 4*0 18 10 10 10 4*0 18 10 10 10 4*0 18 10 10 10 4*0 18 10 10 10 4*0 18 10 10 10
  //   4*0 18 21*10 18 18 18 10 10 10 0 0 0 18 18 8*0 8*18 16*10 32*0 4*10 12*0 16*18 9*0 18 0 e0 64*18 10
  //   10 10 18 10 10 10 4*0 18 10 10 10 4*0 18 10 10 10 4*0 18 10 10 10 4*0 18 10 10 10 4*0 18 10 10 10
  //   4*0 18 21*10 18 18 18 10 10 10 0 0 0 18 18 8*0 8*18 16*10 32*0 4*10 12*0 16*18 9*0 18 0 e0 64*18 10
  //   10 10 18 10 10 10 4*0 18 10 10 10 4*0 18 10 10 10 4*0 18 10 10 10 4*0 18 10 10 10 4*0 18 10 10 10
  //   4*0 18 21*10 18 18 18 10 10 10 0 0 0 18 18 8*0 8*18 16*10 32*0 4*10 12*0 16*18 9*0 18 0 e0 64*18 10
  //   10 10 18 10 10 10 4*0 18 10 10 10 4*0 18 10 10 10 4*0 18 10 10 10 4*0 18 10 10 10 4*0 18 10 10 10
  //   4*0 18 21*10 18 18 18 10 10 10 0 0 0 18 18 8*0 8*18 16*10 32*0 4*10 12*0 16*18 9*0 18 0 e0 64*18 10
  //   10 10 513*18 a a a 10 0 10 10 18 b b b 10 0 10 10 18 0 0 0 10 0 10 10 18 1 1 1 10 0 10 10 18 2 2 2
  //   10 0 10 10 18 5 5 5 10 0 10 10 18 4*c 4*8 4*9 4*3 5 5 4 4 0 18 18 18 4*0 10 10 18 18 8*10 24*18 4*0
  //   12*10 4*0 8*10 0 0 10 10 18 0 0 18 0 0 4*10 0 0 4*10 16*18 9*0 18 0 0 64*18 0 5 18 18 a a a 10 0 10
  //   10 18 b b b 10 0 10 10 18 0 0 0 10 0 10 10 18 1 1 1 10 0 10 10 18 2 2 2 10 0 10 10 18 5 5 5 10 0 10
  //   10 18 4*c 4*8 4*9 4*3 5 5 4 4 0 18 18 18 4*0 10 10 18 18 8*10 24*18 4*0 12*10 4*0 8*10 0 0 10 10 18
  //   0 0 18 0 0 4*10 0 0 4*10 16*18 9*0 18 0 0 64*18 0 5 18 18 a a a 10 0 10 10 18 b b b 10 0 10 10 18 0
  //   0 0 10 0 10 10 18 1 1 1 10 0 10 10 18 2 2 2 10 0 10 10 18 5 5 5 10 0 10 10 18 4*c 4*8 4*9 4*3 5 5 4
  //   4 0 18 18 18 4*0 10 10 18 18 8*10 24*18 4*0 12*10 4*0 8*10 0 0 10 10 18 0 0 18 0 0 4*10 0 0 4*10
  //   16*18 9*0 18 0 0 64*18 0 5 18 18 a a a 10 0 10 10 18 b b b 10 0 10 10 18 0 0 0 10 0 10 10 18 1 1 1
  //   10 0 10 10 18 2 2 2 10 0 10 10 18 5 5 5 10 0 10 10 18 4*c 4*8 4*9 4*3 5 5 4 4 0 18 18 18 4*0 10 10
  //   18 18 8*10 24*18 4*0 12*10 4*0 8*10 0 0 10 10 18 0 0 18 0 0 4*10 0 0 4*10 16*18 9*0 18 0 0 64*18 0 5
  //   18 18 a a a 10 0 10 10 18 b b b 10 0 10 10 18 0 0 0 10 0 10 10 18 1 1 1 10 0 10 10 18 2 2 2 10 0 10
  //   10 18 5 5 5 10 0 10 10 18 4*c 4*8 4*9 4*3 5 5 4 4 0 18 18 18 4*0 10 10 18 18 8*10 24*18 4*0 12*10
  //   4*0 8*10 0 0 10 10 18 0 0 18 0 0 4*10 0 0 4*10 16*18 9*0 18 0 0 64*18 0 5 18 18 a a a 10 0 10 10 18
  //   b b b 10 0 10 10 18 0 0 0 10 0 10 10 18 1 1 1 10 0 10 10 18 2 2 2 10 0 10 10 18 5 5 5 10 0 10 10 18
  //   4*c 4*8 4*9 4*3 5 5 4 4 0 18 18 18 4*0 10 10 18 18 8*10 24*18 4*0 12*10 4*0 8*10 0 0 10 10 18 0 0 18
  //   0 0 4*10 0 0 4*10 16*18 9*0 18 0 0 64*18 0 5 517*18 a 10 a0 e0 4*18 b 10 a0 e0 4*18 0 10 a0 e0 4*18
  //   1 10 a0 e0 4*18 2 10 a0 e0 18 0 0 0 5 10 a5 e5 18*18 5 18 4 0 18 18 18 3 3 3 10 a0 e0 18 18 8*e0
  //   24*18 4*10 4*a0 4*e0 4*18 4*10 4*a0 4*e0 10 10 e0 e0 4*18 10 10 a0 a0 e0 e0 10 10 a0 a0 e0 e0 16*18
  //   90 10 10 90 10 90 10 90 90 18 10 11 71*18 a 10 a0 e0 4*18 b 10 a0 e0 4*18 0 10 a0 e0 4*18 1 10 a0 e0
  //   4*18 2 10 a0 e0 18 0 0 0 5 10 a5 e5 18*18 5 18 4 0 18 18 18 3 3 3 10 a0 e0 18 18 8*e0 24*18 4*10
  //   4*a0 4*e0 4*18 4*10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
  //   contents of PROGRAM (hex, n*v repeats v):
  //   9a 1 1 80 0 20 81 0 20 7f b ba 17 0 80 0 20 fc 33 b3 b 0 ff 48 fc 0 bb 8165*ff
endmodule
