// Logisim project sequencer_test.circ as structural Verilog: 1 circuit, main circuit main
module main (
  input  [7:0] in_1,
  input  \continue ,
  input  enint,
  input  disint,
  input  reset,
  input  request,
  output [7:0] out_7
);

  wire and_2_out, clock_1_out, d_ff_1_q, d_ff_2_q, d_ff_2_qn, nand_1_out, nand_2_out, nand_3_out, nand_4_out,
       nand_5_out, nor_1_out, not_1_out, not_2_out, not_3_out;
  wire [3:0] adder_1_out, and_1_out, bit_extender_1_out, register_1_q;
  wire [7:0] and_3_out, register_2_q;

  Clock clock_1 (.out(clock_1_out));
  Adder #(.width(4)) adder_1 (.a(register_1_q), .b(4'b0000), .out(adder_1_out), .cin(1'b1));  // open: cout
  nand nand_1 (nand_1_out, enint, clock_1_out);
  nand nand_2 (nand_2_out, disint, clock_1_out);
  not not_1 (not_1_out, request);
  assign and_1_out = adder_1_out & bit_extender_1_out;  // AND_Gate and_1, 4 bits wide
  assign bit_extender_1_out = {{3{\continue }}, \continue };  // Bit_Extender bit_extender_1
  not not_2 (not_2_out, nand_1_out);
  D_Flip_Flop d_ff_1 (.D(1'b0), .clk(1'b0), .Q(d_ff_1_q), .preset(not_2_out), .reset(not_3_out));  // open: Qn
  not not_3 (not_3_out, and_2_out);
  and and_2 (and_2_out, nand_2_out, ~reset);  // AND_Gate
  Register #(.trigger("falling"), .width(4)) register_1 (
    .D(and_1_out), .clk(clock_1_out), .Q(register_1_q));  // open: en, clr
  D_Flip_Flop #(.trigger("falling")) d_ff_2 (
    .D(nand_3_out), .clk(clock_1_out), .Q(d_ff_2_q), .Qn(d_ff_2_qn), .preset(reset));  // open: reset
  nand nand_3 (nand_3_out, d_ff_1_q, ~not_1_out);  // NAND_Gate
  nor nor_1 (nor_1_out, register_1_q[3], register_1_q[2], register_1_q[1], register_1_q[0]);
  nand nand_4 (nand_4_out, nor_1_out, clock_1_out);
  and and_3 (and_3_out[0], in_1[0], d_ff_2_q);
  and and_4 (and_3_out[1], in_1[1], d_ff_2_q);
  and and_5 (and_3_out[2], in_1[2], d_ff_2_q);
  and and_6 (and_3_out[3], in_1[3], d_ff_2_q);
  or or_1 (and_3_out[4], in_1[4], d_ff_2_qn);
  or or_2 (and_3_out[5], in_1[5], d_ff_2_qn);
  or or_3 (and_3_out[6], in_1[6], d_ff_2_qn);
  or or_4 (and_3_out[7], in_1[7], d_ff_2_qn);
  nand nand_5 (nand_5_out, nand_4_out, nand_4_out);
  Register register_2 (.D(and_3_out), .clk(nand_5_out), .Q(register_2_q), .clr(reset));  // open: en
  Register register_3 (.D(register_2_q), .clk(nand_4_out), .Q(out_7), .clr(reset));  // open: en
endmodule
